# Fritzing sketch MP3DoorBell (saved by Fritzing 0.9.3b)
breadboards: 1

parts:
  DFPlayer_Mini1 = DFPlayer MINI [package="DIP (Dual Inline) [THT]"]
  Часть1 = Arduino Nano (Rev3.0)
  R1 = Resistor [tolerance=±5% resistance=220 package=THT]
  LED1 = LED - 5mm [color="Red (633nm)" package="5 mm [THT]"]
  R2 = Resistor [tolerance=±5% resistance=1k package=THT]
  R3 = Resistor [tolerance=±5% resistance=1k package=THT]
  S1 = Pushbutton [package="[THT]"]
  R4 = Resistor [tolerance=±5% resistance=10k package=THT]

nets:
  VCC: DFPlayer_Mini1.VCC, Часть1.5V, S1.Pin_3, S1.Pin_4, R4.Pin_1
  N1: DFPlayer_Mini1.RX, R2.Pin_0
  N2: DFPlayer_Mini1.TX, R3.Pin_0
  N3: DFPlayer_Mini1.GND#6, Часть1.GND, LED1.cathode
  N4: DFPlayer_Mini1.BUSY, R1.Pin_0
  N5: Часть1.D2, S1.Pin_1, S1.Pin_2, R4.Pin_0
  N6: Часть1.D10, R3.Pin_1
  N7: Часть1.D11/MOSI, R2.Pin_1
  N8: R1.Pin_1, LED1.anode

custom parts:
  DFPlayer MINI: MP3 module by DFRobot.com for playing Music from an SD-Card. Supports WAV and MP3 files.
